// Logisim project ex2.circ as structural Verilog: 1 circuit, main circuit compute_BrUn
module compute_BrUn (
  input  [31:0] INSTRUCTION,
  output BrUn
);

  and and_1 (BrUn, 1'b1, INSTRUCTION[13]);
endmodule
